// Logisim project test.circ as structural Verilog: 1 circuit, main circuit main
module main (
  input  STEP,
  input  DIR,
  output B_minus,
  output B_plus,
  output A_plus,
  output A_minus,
  output A_plus_2,
  output A_minus_2,
  output B_minus_2,
  output B_plus_2,
  output A_plus_3,
  output A_minus_3,
  output B_plus_3,
  output B_minus_3
);

  wire clock_1_out, clock_2_out, xor_1_out, xor_2_out, xor_3_out, xor_4_out;

  Clock clock_1 (.out(clock_1_out));
  Clock clock_2 (.out(clock_2_out));
  D_Flip_Flop d_ff_1 (.clk(clock_1_out), .D(A_plus), .Q(B_plus), .Qn(B_minus));  // open: preset, en, reset
  D_Flip_Flop d_ff_2 (.clk(clock_2_out), .D(B_minus_2), .Q(A_minus_2), .Qn(A_plus_2));  // open: preset, en, reset
  xor xor_1 (xor_1_out, 1'b1, DIR);
  xor xor_2 (xor_2_out, A_plus_3, B_minus_3);
  D_Flip_Flop d_ff_3 (.clk(clock_1_out), .D(B_plus), .Q(A_minus), .Qn(A_plus));  // open: preset, en, reset
  D_Flip_Flop d_ff_4 (.clk(clock_2_out), .D(A_minus_2), .Q(B_plus_2), .Qn(B_minus_2));  // open: preset, en, reset
  xor xor_3 (xor_3_out, xor_1_out, xor_2_out);
  xor xor_4 (xor_4_out, xor_2_out, DIR);
  T_Flip_Flop t_ff_1 (.clk(STEP), .T(xor_3_out), .Q(A_plus_3), .Qn(A_minus_3));  // open: preset, reset, en
  T_Flip_Flop t_ff_2 (.clk(STEP), .T(xor_4_out), .Q(B_plus_3), .Qn(B_minus_3));  // open: preset, reset, en

  // Notes on the sheet:
  //   clockwise >>> A+ >>> A+/B- >>> B- >>> B-/A- >>> A- >>> A-/B+ >>> B+ >>> B+/A+ 
endmodule
